// Logisim project sr_latch.circ as structural Verilog: 2 circuits, main circuit main
module main (
  output Q,
  output Q2
);

  wire R_out, S_out;

  Button S (.out(S_out));
  Button R (.out(R_out));
  nor nor_1 (Q, S_out, Q2);
  nor nor_2 (Q2, Q, R_out);

  // Notes on the sheet:
  //   SR Latch
endmodule

module d_latch (
  input  Set,
  input  Enable,
  output Q
);

  wire and_1_out, and_2_out, nor_2_out, not_1_out;

  not not_1 (not_1_out, Set);
  and and_1 (and_1_out, not_1_out, Enable);
  and and_2 (and_2_out, Enable, Set);
  nor nor_1 (Q, and_1_out, nor_2_out);
  nor nor_2 (nor_2_out, Q, and_2_out);

  // Notes on the sheet:
  //   D Latch
endmodule
